// Logisim project cpu.circ as structural Verilog: 1 circuit, main circuit main
module main (
  input  [31:0] INSTRUCTION,
  input  CLOCK,
  output [31:0] PROGRAM_COUNTER,
  output [31:0] ra,
  output [31:0] sp,
  output [31:0] t0,
  output [31:0] t1,
  output [31:0] t2,
  output [31:0] s0,
  output [31:0] s1,
  output [31:0] a0
);

  wire branch_comp_1_breq, branch_comp_1_brlt, control_logic_1_asel, control_logic_1_brun,
       control_logic_1_bsel, control_logic_1_memrw, control_logic_1_regwen;
  wire [1:0] control_logic_1_wbsel;
  wire [2:0] control_logic_1_immsel, funct3;
  wire [3:0] control_logic_1_alusel;
  wire [4:0] rd, rs1, rs2;
  wire [6:0] funct7, opcode;
  wire [31:0] adder_1_out, Arithmetic_Logic_Unit_result, DMEM_p3, imm_gen_1_imm, multiplexer_1_out,
       multiplexer_2_out, multiplexer_3_out, RegFile_read_data_1, RegFile_read_data_2;

  control_logic control_logic_1 (
    .BSel(control_logic_1_bsel), .RegWEn(control_logic_1_regwen), .ASel(control_logic_1_asel),
    .ImmSel(control_logic_1_immsel), .BrUn(control_logic_1_brun), .BrLt(branch_comp_1_brlt),
    .BrEq(branch_comp_1_breq), .inst({funct7, rs2, rs1, funct3, rd, opcode}),
    .ALUSel(control_logic_1_alusel), .MemRW(control_logic_1_memrw), .WBSel(control_logic_1_wbsel));  // open: PCSel
  Adder #(.width(32)) adder_1 (.a(PROGRAM_COUNTER), .b(32'h4), .out(adder_1_out));  // open: cin, cout
  // Probe on rs1
  Register #(.width(32)) PC (.D(adder_1_out), .clk(CLOCK), .Q(PROGRAM_COUNTER));  // open: en, clr
  Register #(.width(32)) register_1 (
    .D(INSTRUCTION), .clk(CLOCK), .Q({funct7, rs2, rs1, funct3, rd, opcode}));  // open: en, clr
  imm_gen imm_gen_1 (
    .ImmSel(control_logic_1_immsel), .imm(imm_gen_1_imm), .inst({funct7, rs2, rs1, funct3, rd, opcode}));
  branch_comp branch_comp_1 (
    .BrEq(branch_comp_1_breq), .BrUn(control_logic_1_brun), .BrLt(branch_comp_1_brlt), .rs2(imm_gen_1_imm));  // open: rs1
  // Probe on control_logic_1_regwen
  regfile_main RegFile (
    .rs2(rs2), .rd(rd), .Read_Data_1(RegFile_read_data_1), .Read_Data_2(RegFile_read_data_2), .ra(ra),
    .sp(sp), .t0(t0), .t1(t1), .t2(t2), .s0(s0), .s1(s1), .a0(a0), .rs1(rs1), .Write_Data(multiplexer_3_out),
    .RegWEn(control_logic_1_regwen), .clk(CLOCK));
  Multiplexer #(.width(32), .enable("false")) multiplexer_1 (
    .in0(RegFile_read_data_1), .out(multiplexer_1_out), .sel(control_logic_1_asel));  // open: in1
  Multiplexer #(.width(32), .enable("false")) multiplexer_2 (
    .in0(imm_gen_1_imm), .in1(RegFile_read_data_2), .out(multiplexer_2_out), .sel(control_logic_1_bsel));
  alu Arithmetic_Logic_Unit (
    .ALUSel(control_logic_1_alusel), .Result(Arithmetic_Logic_Unit_result), .A(multiplexer_1_out),
    .B(multiplexer_2_out));
  // Probe on Arithmetic_Logic_Unit_result
  // mem_main DMEM: pin names not known; wires that end beside it: CLOCK, control_logic_1_memrw, DMEM_p3
  // Probe on multiplexer_3_out
  Multiplexer #(.select(2), .width(32), .enable("false")) multiplexer_3 (
    .in0(Arithmetic_Logic_Unit_result), .in1(DMEM_p3), .in2(adder_1_out), .out(multiplexer_3_out),
    .sel(control_logic_1_wbsel));  // open: in3

  // Other names for the same wires on the sheet: clk = CLOCK

  // Notes on the sheet:
  //   Output
  //   IMEM (do **NOT** move this)
  //   Inputs
  //   Inputs/Outputs for testing. Do **NOT** move these.
endmodule
